// Logisim project converter_nand_nor.circ as structural Verilog: 1 circuit, main circuit main
module main (
  input  a,
  input  b,
  input  c,
  input  d,
  input  e,
  output A_N,
  output B_N,
  output C_N,
  output D_N,
  output A_R,
  output B_R,
  output C_R,
  output D_R
);

  wire nand_1_out, nand_2_out, nand_3_out, nand_4_out, nand_5_out, nand_6_out, nand_7_out, nand_8_out,
       nand_9_out, nand_10_out, nand_11_out, nand_12_out, nand_13_out, nand_14_out, nand_15_out, nor_1_out,
       nor_2_out, nor_3_out, nor_4_out, nor_5_out, nor_6_out, nor_7_out, nor_8_out, nor_9_out, nor_11_out,
       nor_12_out, nor_13_out, nor_14_out, nor_15_out;

  nand nand_1 (nand_1_out, a, e);
  nand nand_2 (nand_2_out, e, e);
  nand nand_3 (nand_3_out, c, c);
  nand nand_4 (nand_4_out, a, a);
  nand nand_5 (nand_5_out, b, b);
  nand nand_6 (nand_6_out, d, d);
  nand nand_7 (nand_7_out, d, e);
  nor nor_1 (nor_1_out, a, a);
  nor nor_2 (nor_2_out, b, e);
  nor nor_3 (nor_3_out, c, d);
  nor nor_4 (nor_4_out, a, e);
  nor nor_5 (nor_5_out, e, e);
  nor nor_6 (nor_6_out, b, c);
  nor nor_7 (nor_7_out, b, b);
  nor nor_8 (nor_8_out, c, c);
  nor nor_9 (nor_9_out, d, d);
  nand nand_8 (nand_8_out, b, c, nand_2_out);
  nand nand_9 (nand_9_out, nand_3_out, d);
  nand nand_10 (nand_10_out, nand_4_out, b, e);
  nand nand_11 (nand_11_out, a, nand_5_out);
  nand nand_12 (nand_12_out, a, nand_3_out, nand_6_out);
  nand nand_13 (nand_13_out, nand_5_out, c);
  nand nand_14 (nand_14_out, b, nand_3_out, nand_6_out, nand_2_out);
  nand nand_15 (nand_15_out, nand_5_out, e);
  nor nor_10 (A_R, nor_1_out, nor_2_out, nor_3_out);
  nor nor_11 (nor_11_out, nor_1_out, nor_5_out);
  nor nor_12 (nor_12_out, nor_7_out, nor_8_out, e);
  nor nor_13 (nor_13_out, c, nor_9_out);
  nor nor_14 (nor_14_out, a, nor_5_out);
  nor nor_15 (nor_15_out, nor_7_out, d, nor_5_out);
  nand nand_16 (A_N, nand_1_out, nand_8_out, nand_9_out);
  nand nand_17 (B_N, nand_10_out, nand_11_out, nand_12_out);
  nand nand_18 (C_N, nand_1_out, nand_13_out, nand_14_out);
  nand nand_19 (D_N, nand_15_out, nand_14_out, nand_8_out, nand_7_out);
  nor nor_16 (B_R, nor_4_out, nor_11_out, nor_6_out, nor_12_out, nor_13_out);
  nor nor_17 (C_R, nor_14_out, nor_6_out, nor_12_out, nor_13_out);
  nor nor_18 (D_R, nor_2_out, nor_15_out, nor_13_out);
endmodule
