// Logisim project moore_fsm.circ as structural Verilog: 1 circuit, main circuit main
module main (
  input  x,
  input  rst,
  output z1,
  output z2,
  output y
);

  wire clk, d1, d2, nx, nz1, t1, t2, t3, t4;

  Clock u_clk (.out(clk));
  not not_1 (nx, x);
  not not_2 (nz1, z1);
  and and_1 (t1, nx, z1);
  and and_2 (t2, x, z2);
  and and_3 (t3, nx, z2);
  and and_4 (t4, x, nz1);
  or or_1 (d1, t1, t2);
  or or_2 (d2, t3, t4);
  or or_3 (y, nz1, z2);
  D_Flip_Flop d_ff_1 (.clk(clk), .D(d1), .Q(z1), .preset(rst));  // open: Qn, en, reset
  D_Flip_Flop d_ff_2 (.clk(clk), .D(d2), .Q(z2), .reset(rst));  // open: Qn, preset, en

  // Other names for the same wires on the sheet: yv = y
endmodule
