// Logisim project converter_draft.circ as structural Verilog: 1 circuit, main circuit main
module main (
  input  a,
  input  b,
  input  c,
  input  d,
  input  e,
  input  a_2,
  input  b_2,
  input  c_2,
  input  d_2,
  input  e_2,
  output out_11,
  output out_12,
  output out_13,
  output out_14,
  output out_15,
  output out_16,
  output out_17,
  output out_18
);

  wire nand_1_out, nand_2_out, nand_3_out, nand_4_out, nand_5_out, nand_6_out, nand_7_out, nand_8_out,
       nand_9_out, nand_10_out, nand_11_out, nand_12_out, nand_13_out, nor_1_out, nor_2_out, nor_3_out,
       nor_4_out, nor_5_out, nor_6_out, nor_8_out, nor_9_out, nor_10_out, nor_11_out, nor_12_out, nor_13_out,
       nor_14_out, nor_15_out, not_1_out, not_2_out, not_3_out, not_4_out, not_5_out, not_6_out, not_7_out,
       not_8_out, not_9_out, not_10_out;

  nand nand_1 (nand_1_out, a, e);
  not not_1 (not_1_out, e);
  not not_2 (not_2_out, c);
  not not_3 (not_3_out, a);
  not not_4 (not_4_out, b);
  not not_5 (not_5_out, d);
  nand nand_2 (nand_2_out, a, e);
  nand nand_3 (nand_3_out, d, e);
  not not_6 (not_6_out, a_2);
  nor nor_1 (nor_1_out, b_2, e_2);
  nor nor_2 (nor_2_out, c_2, d_2);
  nor nor_3 (nor_3_out, a_2, e_2);
  not not_7 (not_7_out, e_2);
  nor nor_4 (nor_4_out, b_2, c_2);
  not not_8 (not_8_out, b_2);
  not not_9 (not_9_out, c_2);
  not not_10 (not_10_out, d_2);
  nor nor_5 (nor_5_out, b_2, c_2);
  nor nor_6 (nor_6_out, b_2, e_2);
  nand nand_4 (nand_4_out, b, c, not_1_out);
  nand nand_5 (nand_5_out, not_2_out, d);
  nand nand_6 (nand_6_out, not_3_out, b, e);
  nand nand_7 (nand_7_out, a, not_4_out);
  nand nand_8 (nand_8_out, a, not_2_out, not_5_out);
  nand nand_9 (nand_9_out, not_4_out, c);
  nand nand_10 (nand_10_out, b, not_2_out, not_5_out, not_1_out);
  nand nand_11 (nand_11_out, not_4_out, e);
  nand nand_12 (nand_12_out, b, not_2_out, not_5_out, not_1_out);
  nand nand_13 (nand_13_out, b, c, not_1_out);
  nor nor_7 (out_15, not_6_out, nor_1_out, nor_2_out);
  nor nor_8 (nor_8_out, not_6_out, not_7_out);
  nor nor_9 (nor_9_out, not_8_out, not_9_out, e_2);
  nor nor_10 (nor_10_out, c_2, not_10_out);
  nor nor_11 (nor_11_out, a_2, not_7_out);
  nor nor_12 (nor_12_out, not_8_out, not_9_out, e_2);
  nor nor_13 (nor_13_out, c_2, not_10_out);
  nor nor_14 (nor_14_out, not_8_out, d_2, not_7_out);
  nor nor_15 (nor_15_out, c_2, not_10_out);
  nand nand_14 (out_11, nand_1_out, nand_4_out, nand_5_out);
  nand nand_15 (out_12, nand_6_out, nand_7_out, nand_8_out);
  nand nand_16 (out_13, nand_2_out, nand_9_out, nand_10_out);
  nand nand_17 (out_14, nand_11_out, nand_12_out, nand_13_out, nand_3_out);
  nor nor_16 (out_16, nor_3_out, nor_8_out, nor_4_out, nor_9_out, nor_10_out);
  nor nor_17 (out_17, nor_11_out, nor_5_out, nor_12_out, nor_13_out);
  nor nor_18 (out_18, nor_6_out, nor_14_out, nor_15_out);
endmodule
