// Logisim project comb_loop.circ as structural Verilog: 1 circuit, main circuit main
module main (
  input  S,
  input  R,
  output Q
);

  wire qn;

  nor nor_1 (Q, R, qn);
  nor nor_2 (qn, S, Q);
endmodule
