// Logisim project d_flipflop.circ as structural Verilog: 1 circuit, main circuit main
module main (
  input  d,
  output q,
  output nq
);

  wire clk;

  Clock u_clk (.out(clk));
  D_Flip_Flop d_ff_1 (.clk(clk), .D(d), .Q(q), .Qn(nq));  // open: preset, en, reset
endmodule
