// Logisim project jk_flipflop.circ as structural Verilog: 1 circuit, main circuit main
module main (
  input  j,
  input  k,
  input  clk,
  input  rst,
  output q,
  output nq
);

  J_K_Flip_Flop j_k_ff_1 (.J(j), .clk(clk), .K(k), .Q(q), .Qn(nq), .reset(rst));  // open: preset, en
endmodule
