// Logisim project misc_parts.circ as structural Verilog: 1 circuit, main circuit main
module main (
  input  [1:0] a,
  input  [1:0] b,
  input  s,
  output [1:0] sum,
  output cout,
  output lt,
  output [1:0] m,
  output d2,
  output x,
  output xn
);

  Adder #(.width(2)) adder_1 (.a(a), .b(b), .out(sum), .cout(cout));  // open: cin
  Comparator #(.width(2), .mode("unsigned")) comparator_1 (.a(a), .b(b), .lt(lt));  // open: gt, eq
  Multiplexer #(.width(2), .enable("false")) multiplexer_1 (.in0(a), .in1(b), .out(m), .sel(s));
  Decoder #(.select(2), .enable("false")) decoder_1 (.out2(d2), .sel(b));  // open: out0, out1, out3
  xor xor_1 (x, 1'b1, a[0]);
  NotExactlyOne xnor_1 (.out(xn), .in0(a[1]), .in1(s), .in2(a[0]));
endmodule
