// Logisim project subcircuit.circ as structural Verilog: 2 circuits, main circuit main
module half (
  input  a,
  input  b,
  output s,
  output c
);

  xor xor_1 (s, a, b);
  and and_1 (c, a, b);
endmodule

module main (
  input  x,
  input  y,
  input  z,
  output s,
  output c1,
  output c2
);

  wire t;

  half half_1 (.a(x), .b(y), .s(t), .c(c1));
  half half_2 (.a(t), .b(z), .s(s), .c(c2));
  // Probe on nothing
endmodule
