// Logisim project width_mismatch.circ as structural Verilog: 1 circuit, main circuit main
module main (
  input  [1:0] a,
  output y
);

  // Pins of 1 and 2 bits meet at a

  assign y = a[0];
endmodule
