// Logisim project wire_through_body.circ as structural Verilog: 1 circuit, main circuit main
module main (
  input  b,
  input  c,
  output z,
  output w
);

  wire undriven;

  nand nand_1 (w, c, undriven);

  assign z = b;
endmodule
