// Logisim project mixed_gates.circ as structural Verilog: 1 circuit, main circuit main
module main (
  input  P,
  input  Q,
  input  R,
  output out_4,
  output out_5
);

  wire and_1_out, and_2_out, and_3_out, and_4_out, and_5_out, not_1_out, not_2_out, not_3_out, not_4_out,
       not_5_out, xor_1_out;

  xor xor_1 (xor_1_out, P, Q);
  not not_1 (not_1_out, P);
  not not_2 (not_2_out, R);
  not not_3 (not_3_out, P);
  not not_4 (not_4_out, Q);
  not not_5 (not_5_out, R);
  and and_1 (and_1_out, xor_1_out, R);
  and and_2 (and_2_out, not_1_out, not_2_out);
  and and_3 (and_3_out, not_3_out, Q);
  and and_4 (and_4_out, P, not_5_out);
  and and_5 (and_5_out, not_4_out, R);
  or or_1 (out_4, and_1_out, and_2_out);
  or or_2 (out_5, and_3_out, and_4_out, and_5_out);
endmodule
