// Logisim project sample_bcd_excess3.circ as structural Verilog: 1 circuit, main circuit main
module main (
  input  a,
  input  b,
  input  c,
  input  d,
  output A_xs3,
  output B_xs3,
  output C_xs3,
  output D_xs3
);

  wire nand_1_out, nand_2_out, nand_3_out, nand_4_out, nand_6_out, nand_7_out, nand_8_out, nand_9_out,
       nand_10_out, nand_11_out;

  nand nand_1 (nand_1_out, b, b);
  nand nand_2 (nand_2_out, b, c);
  nand nand_3 (nand_3_out, b, d);
  nand nand_4 (nand_4_out, c, c);
  nand nand_5 (D_xs3, d, d);
  nand nand_6 (nand_6_out, c, d);
  nand nand_7 (nand_7_out, a, nand_1_out);
  nand nand_8 (nand_8_out, nand_1_out, c);
  nand nand_9 (nand_9_out, nand_1_out, d);
  nand nand_10 (nand_10_out, b, nand_4_out, D_xs3);
  nand nand_11 (nand_11_out, nand_4_out, D_xs3);
  nand nand_12 (A_xs3, nand_7_out, nand_2_out, nand_3_out);
  nand nand_13 (B_xs3, nand_8_out, nand_9_out, nand_10_out);
  nand nand_14 (C_xs3, nand_11_out, nand_6_out);
endmodule
